# Fritzing sketch ir-station Sketch (saved by Fritzing 0.9.5d)

parts:
  Raspberry_Pi1 = Raspberry Pi B+
  LCD1 = LCD screen
  LCM1602_IIC1 = LCM1602 IIC [part_number="LCM1602 IIC" chip_label="LCM1602 IIC" package="DIP (Dual Inline) [THT]"]
  M1 = MT3608 Module
  A1 = MAX6675 module [package=THT]
  A2 = MAX6675 module [package=THT]
  Halogen_Lapm1 = Halogen Lamp G4 [package="4 mm [THT]"]
  A3 = ceramic infrared heater
  A4 = Noyito LR7843 mosfet pwm driver
  A5 = Noyito LR7843 mosfet pwm driver
  RY1 = SSR-FOTEK [part_number=SSR-40DA-FOTEK]
  J3 = Camdenboss CTB0158-10 [part_number=CTB0158-10 package=THT]
  F1 = FUSE [package=fuse_5mm]
  RE1 = KY-040 Rotary encoder [package="Breakout board"]
  RY2 = SSR-FOTEK [part_number=SSR-40DA-FOTEK]
  Halogen_Lapm2 = Halogen Lamp G4 [package="4 mm [THT]"]
  Halogen_Lapm3 = Halogen Lamp G4 [package="4 mm [THT]"]
  Halogen_Lapm4 = Halogen Lamp G4 [package="4 mm [THT]"]
  Halogen_Lapm5 = Halogen Lamp G4 [package="4 mm [THT]"]
  Halogen_Lapm6 = Halogen Lamp G4 [package="4 mm [THT]"]
  Halogen_Lapm7 = Halogen Lamp G4 [package="4 mm [THT]"]
  Halogen_Lapm8 = Halogen Lamp G4 [package="4 mm [THT]"]
  Halogen_Lapm9 = Halogen Lamp G4 [package="4 mm [THT]"]
  J4 = Camdenboss CTB0158-10 [part_number=CTB0158-10 package=THT]
  Mod1 = generic-ac-power-supply [package=THT]
  F2 = Fan - Ventilador [package=THT]
  LED1 = LED - 3mm [color="Red (633nm)" package="3 mm [THT]"]
  LED2 = LED - 3mm [color="Green (560nm)" package="3 mm [THT]"]
  R1 = Resistor [tolerance=±5% resistance=1k package="2512 [SMD]"]
  S2 = Pushbutton [package="[THT]"]
  S3 = Pushbutton [package="[THT]"]
  S4 = Pushbutton [package="[THT]"]
  R2 = Resistor [tolerance=±5% resistance=22k package="2512 [SMD]"]
  R3 = Resistor [tolerance=±5% resistance=680 package="2512 [SMD]"]
  R4 = Resistor [tolerance=±5% resistance=22k package="2512 [SMD]"]
  R5 = Resistor [tolerance=±5% resistance=680 package="2512 [SMD]"]
  R6 = Resistor [tolerance=±5% resistance=22k package="2512 [SMD]"]
  R7 = Resistor [tolerance=±5% resistance=680 package="2512 [SMD]"]
  J5 = Camdenboss CTB0158-2 [part_number=CTB0158-2 package=THT]
  J7 = Camdenboss CTB0158-2 [part_number=CTB0158-2 package=THT]
  S7 = Round Pushbutton
  S8 = Round Pushbutton
  S9 = illuminated rocker switch [package=THT]
  S10 = illuminated rocker switch [package=THT]

nets:
  N1: Raspberry_Pi1.GPIO2, LCM1602_IIC1.SDA
  N2: Raspberry_Pi1.GPIO3, LCM1602_IIC1.SCL
  N3: Raspberry_Pi1.GPIO4, J3.terminal_8, J4.terminal_8
  3V3: Raspberry_Pi1.3V3, RE1.Vcc, R2.Pin_1, R4.Pin_1, R6.Pin_1
  N4: Raspberry_Pi1.GPIO10, RE1.SW
  N5: Raspberry_Pi1.GPIO9, RE1.CLK
  N6: Raspberry_Pi1.GPIO11, RE1.DT
  GND: Raspberry_Pi1.GND, LCM1602_IIC1.GND, RE1.GND, R1.Pin_0, S2.Pin_3, S2.Pin_4, S4.Pin_1, S4.Pin_2, R2.Pin_0, R7.Pin_0
  N7: Raspberry_Pi1.GPIO13, A4.Pin_5, A4.Pin_7, J3.terminal_3, J4.terminal_3
  N8: Raspberry_Pi1.GPIO19, LED2.anode
  N9: Raspberry_Pi1.GPIO26, LED1.anode
  N10: Raspberry_Pi1.GPIO21, R7.Pin_1
  N11: Raspberry_Pi1.GPIO20, R5.Pin_1
  N12: Raspberry_Pi1.GPIO16, R3.Pin_1
  N13: Raspberry_Pi1.GPIO12, A5.Pin_7, J3.terminal_5, J4.terminal_5
  N14: Raspberry_Pi1.GPIO8, A1.pin5, J3.terminal_7, J4.terminal_7
  N15: Raspberry_Pi1.GPIO25, A2.pin5, J3.terminal_4, J4.terminal_4
  N16: Raspberry_Pi1.GPIO24, A1.pin3, A2.pin3, J3.terminal_6, J4.terminal_6
  5V: Raspberry_Pi1.5V, LCM1602_IIC1.VCC
  VSS: LCD1.VSS, LCM1602_IIC1.VSS
  VDD: LCD1.VDD, LCM1602_IIC1.VDD
  N17: LCD1.V0, LCM1602_IIC1.V0
  N18: LCD1.RS, LCM1602_IIC1.RS
  N19: LCD1.R/W, LCM1602_IIC1.RW
  N20: LCD1.E, LCM1602_IIC1.E
  N21: LCD1.DB0, LCM1602_IIC1.D0
  N22: LCD1.DB1, LCM1602_IIC1.D1
  N23: LCD1.DB2, LCM1602_IIC1.D2
  N24: LCD1.DB3, LCM1602_IIC1.D3
  N25: LCD1.DB4, LCM1602_IIC1.D4
  N26: LCD1.DB5, LCM1602_IIC1.D5
  N27: LCD1.DB6, LCM1602_IIC1.D6
  N28: LCD1.DB7, LCM1602_IIC1.D7
  N29: LCD1.LED+, LCM1602_IIC1.A
  N30: LCD1.LED-, LCM1602_IIC1.K
  N31: M1.pin3, A5.Pin_1, J3.pin10, J3.terminal_10, J4.terminal_10, F2.5V
  N32: M1.pin4, A4.Pin_3, A4.Pin_4, A4.Pin_6, A5.Pin_3, A5.Pin_4, A5.Pin_6, J3.terminal_9, J4.terminal_9, S7.leg0, S8.leg1, S10.pin2
  N33: A1.pin1, A2.pin1
  N34: A1.pin2, A2.pin2
  N35: A1.pin4, A2.pin4
  N36: Halogen_Lapm1.Pin1, RY2.Pin_1, Halogen_Lapm4.Pin1, Halogen_Lapm7.Pin1
  N37: Halogen_Lapm1.Pin2, Halogen_Lapm2.Pin1
  N38: A3.Pin_1, RY1.Pin_1
  N39: A3.Pin_2, F1.1, Halogen_Lapm3.Pin2, Halogen_Lapm6.Pin2, Halogen_Lapm9.Pin2
  N40: A4.Pin_1, RY1.Pin_3, RY2.Pin_3
  N41: A4.Pin_2, RY1.Pin_4, S7.leg1
  N42: A5.Pin_2, RY2.Pin_4, S8.leg0
  N43: RY1.Pin_2, RY2.Pin_2, S9.pin1
  N44: J3.terminal_1, J4.terminal_1, Mod1.pin3#3
  N45: J3.terminal_2, J4.terminal_2, Mod1.pin3#2
  N46: F1.2, J7.terminal_2, S9.pin3
  N47: Halogen_Lapm2.Pin2, Halogen_Lapm3.Pin1
  N48: Halogen_Lapm4.Pin2, Halogen_Lapm5.Pin1
  N49: Halogen_Lapm5.Pin2, Halogen_Lapm6.Pin1
  N50: Halogen_Lapm7.Pin2, Halogen_Lapm8.Pin1
  N51: Halogen_Lapm8.Pin2, Halogen_Lapm9.Pin1
  N52: Mod1.pin1, J5.terminal_1
  N53: Mod1.pin2, J5.terminal_2
  N54: F2.GND, S10.pin1
  N55: LED2.cathode, R1.Pin_1
  N56: S2.Pin_1, S2.Pin_2, R3.Pin_0
  N57: S3.Pin_1, S3.Pin_2, R5.Pin_0
  N58: S3.Pin_3, S3.Pin_4, R4.Pin_0
  N59: S4.Pin_3, S4.Pin_4, R6.Pin_0
  N60: J7.terminal_1, S9.pin2

notes:
  220V
  Connector
  GX16-10L
  Top heater
  450 W
  Bottom heater
  3400 W
  Start
  Stop
  Shutdown
  5V 5A
  12V
  Top thermometer
  Bottom thermometer

custom parts:
  LCM1602 IIC: I2C-Module to use a 1602 or 2004 LCD on with the wire.h libory Serial LCD Modul
  MT3608 Module: MT3608 Boost Converter Module Links: Aerosemi MT3608 2A Step Up Converter datasheet
  MAX6675 module: MAX6675 Module + K Type Thermocouple Sensor Temperature Degrees.
  Halogen Lamp G4: A generic Halogen Lamp with G4 socket. Typical operating voltage around 12v and power around 20W
  ceramic infrared heater: ceramic infrared heater.
  Noyito LR7843 mosfet pwm driver: This MOSFET module with optoisolation uses the LR7843 N-Channel logic compatible MOSFET with ultra low Rds(on) for moderate to higher current low-side switching applications of up to 15A continuous.
  SSR-FOTEK: Solid State Relay, SSR-40DA Links: SSR-40DA Datasheet
  KY-040 Rotary encoder: KY-040 Rotary Encoder with switch on breakout borad from AZ Delivery
  generic-ac-power-supply: Generic ac power supply module. Use as is, or customize the svgs to fit your particular device (as they are all different.) Provides AC input and single DC output. PCB is generic and will need modifications if you intend to do a pcb mount.
  Fan - Ventilador: Ventilador de 2 pines, se encuentra comunmente en computadoras de escritorio
  illuminated rocker switch: illuminated rocker switch.
